# Fritzing sketch GearIndicator (saved by Fritzing 0.9.0b)
breadboards: 1

parts:
  Part1 = Arduino Pro Mini v13
  R1 = Trimmer Potentiometer [maximum_resistance=10kΩ package=THT]
  R2 = Resistor [tolerance=±5% resistance=220 package=THT]
  LED1 = LED - 5mm [color="Red (633nm)" package="5 mm [THT]"]
  LED3 = LED - 5mm [color="Red (633nm)" package="5 mm [THT]"]
  LED4 = LED - 5mm [color="Red (633nm)" package="5 mm [THT]"]
  LED5 = LED - 5mm [color="Red (633nm)" package="5 mm [THT]"]
  S1 = Momentary Switch [package=ksa_sealed_tac_switch]
  LED6 = LED - 5mm [color="Red (633nm)" package="5 mm [THT]"]
  LED2 = LED - 5mm [color="Red (633nm)" package="5 mm [THT]"]

nets:
  N1: Part1.GND, R1.leg1, S1.1, S1.2
  N2: Part1.VCC, R1.leg2
  N3: Part1.A1, R1.wiper
  N4: Part1.D9_PWM, R2.Pin_1
  N5: Part1.D8, S1.3, S1.4
  N6: Part1.D7, LED1.anode
  N7: Part1.D6_PWM, LED2.anode
  N8: Part1.D5_PWM, LED3.anode
  N9: Part1.D4, LED4.anode
  N10: Part1.D3_PWM, LED5.anode
  N11: Part1.D2, LED6.anode
  N12: R2.Pin_0, LED1.cathode, LED3.cathode, LED4.cathode, LED5.cathode, LED6.cathode, LED2.cathode
